// Logisim project oi.circ as structural Verilog: 1 circuit, main circuit main
module main (
  input  C,
  input  A,
  input  in_3,
  input  B,
  input  in_5,
  output out_6,
  output out_7,
  output out_8,
  output out_9
);

  wire adder_1_cout, adder_1_out, adder_2_out;

  Adder #(.width(1)) adder_1 (.a(in_5), .b(in_3), .out(adder_1_out), .cout(adder_1_cout));  // open: cin
  Adder #(.width(1)) adder_2 (.a(B), .b(A), .out(adder_2_out), .cin(adder_1_cout), .cout(out_9));
  Adder #(.width(1)) adder_3 (.a(adder_1_out), .b(adder_2_out), .out(out_7), .cin(out_6), .cout(out_8));
  Adder adder_4 ();  // open: a, b, out, cin, cout
endmodule
